// Logisim project debugging_not_dff_tmr.circ as structural Verilog: 1 circuit, main circuit main
module main (
  input  clk,
  input  a
);

  wire d_ff_1_q, d_ff_2_q, d_ff_3_q;

  D_Flip_Flop d_ff_1 (.D(a), .clk(clk), .Q(d_ff_1_q));  // open: Qn, preset, reset
  D_Flip_Flop d_ff_2 (.D(a), .clk(clk), .Q(d_ff_2_q));  // open: Qn, preset, reset
  D_Flip_Flop d_ff_3 (.D(a), .clk(clk), .Q(d_ff_3_q));  // open: Qn, preset, reset
  // NOT_Gate not_1 has open pins: in=d_ff_1_q, out=open
  // NOT_Gate not_2 has open pins: in=d_ff_2_q, out=open
  // NOT_Gate not_3 has open pins: in=d_ff_3_q, out=open
endmodule
