// Logisim project not_gate_triplicate.circ as structural Verilog: 1 circuit, main circuit main
module main (
  input  a,
  input  clk,
  output o
);

  wire not_1_out;

  not not_1 (not_1_out, a);
  D_Flip_Flop d_ff_1 (.D(not_1_out), .clk(clk), .Q(o));  // open: Qn, preset, reset
endmodule
