// Logisim project simple_tmr.circ as structural Verilog: 2 circuits, main circuit main
module main (
  input  in_1,
  input  in_2,
  output out_3,
  output out_4
);

  wire d_ff_1_q, d_ff_2_q, d_ff_3_q, not_1_out, not_2_out, not_3_out;

  D_Flip_Flop d_ff_1 (.D(not_1_out), .clk(in_2), .Q(d_ff_1_q));  // open: Qn, preset, reset
  not not_1 (not_1_out, in_1);
  D_Flip_Flop d_ff_2 (.D(not_2_out), .clk(in_2), .Q(d_ff_2_q));  // open: Qn, preset, reset
  not not_2 (not_2_out, in_1);
  D_Flip_Flop d_ff_3 (.D(not_3_out), .clk(in_2), .Q(d_ff_3_q));  // open: Qn, preset, reset
  not not_3 (not_3_out, in_1);
  majority majority_1 (.a(d_ff_1_q), .b(d_ff_2_q), .c(d_ff_3_q), .outt(out_3), .err(out_4));
endmodule

module majority (
  input  a,
  input  b,
  input  c,
  output outt,
  output err
);

  wire and0_out, and1_out, and2_out, and3_out, and4_out, and5_out, not0_out, not1_out, not2_out, or0_out,
       or1_out;

  not not0 (not0_out, a);
  not not1 (not1_out, b);
  not not2 (not2_out, c);
  and and0 (and0_out, b, c);
  or or0 (or0_out, and0_out, and1_out);
  and and1 (and1_out, a, c);
  and and4 (and4_out, a, b);
  and and2 (and2_out, not0_out, c);
  or or1 (or1_out, and2_out, and3_out);
  and and3 (and3_out, a, not1_out);
  and and5 (and5_out, b, not2_out);
  or or2 (outt, or0_out, and4_out);
  or or3 (err, or1_out, and5_out);
endmodule
