// Logisim project test_not_dff_tmr.circ as structural Verilog: 1 circuit, main circuit main
module main (
  input  i_a,
  input  i_clk,
  input  in_3,
  output outt,
  output err
);

  wire and0_out, and1_out, and2_out, and3_out, and4_out, and5_out, d_ff_1_q, d_ff_2_q, d_ff_3_q, d_ff_4_q,
       not0_out, not1_out, not2_out, not_1_out, not_2_out, not_3_out, not_4_out, or0_out, or1_out;

  D_Flip_Flop d_ff_1 (.D(in_3), .Q(d_ff_1_q));  // open: clk, Qn, preset, reset
  D_Flip_Flop d_ff_2 (.D(i_a), .clk(i_clk), .Q(d_ff_2_q));  // open: Qn, preset, reset
  D_Flip_Flop d_ff_3 (.D(i_a), .clk(i_clk), .Q(d_ff_3_q));  // open: Qn, preset, reset
  D_Flip_Flop d_ff_4 (.D(i_a), .clk(i_clk), .Q(d_ff_4_q));  // open: Qn, preset, reset
  not not_1 (not_1_out, d_ff_1_q);
  not not_2 (not_2_out, d_ff_2_q);
  not not_3 (not_3_out, d_ff_3_q);
  not not_4 (not_4_out, d_ff_4_q);
  not not0 (not0_out, not_2_out);
  not not1 (not1_out, not_3_out);
  not not2 (not2_out, not_4_out);
  and and0 (and0_out, not_3_out, not_4_out);
  and and1 (and1_out, not_2_out, not_4_out);
  and and2 (and2_out, not0_out, not_4_out);
  and and3 (and3_out, not_2_out, not1_out);
  or or0 (or0_out, and0_out, and1_out);
  and and4 (and4_out, not_2_out, not_3_out);
  or or1 (or1_out, and2_out, and3_out);
  and and5 (and5_out, not_3_out, not2_out);
  or or2 (outt, or0_out, and4_out);
  or or3 (err, or1_out, and5_out);
endmodule
